// Logisim project logisim_alu.circ as structural Verilog: 1 circuit, main circuit main
module main (
  input  [15:0] A,
  input  [15:0] B,
  input  [15:0] OUTPUT,
  input  [3:0] OPCODE
);

  wire [15:0] adder_1_out, and_1_out, nand_1_out, nor_1_out, not_1_out, or_1_out, subtractor_1_out, xor_1_out;

  Adder #(.width(16)) adder_1 (.a(A), .b(B), .out(adder_1_out));  // open: cin, cout
  Subtractor #(.width(16)) subtractor_1 (.a(A), .b(B), .out(subtractor_1_out));  // open: bin, bout
  assign and_1_out = A & B;  // AND_Gate and_1, 16 bits wide
  assign or_1_out = A | B;  // OR_Gate or_1, 16 bits wide
  assign xor_1_out = A ^ B;  // XOR_Gate xor_1, 16 bits wide
  assign nand_1_out = ~(A & B);  // NAND_Gate nand_1, 16 bits wide
  assign nor_1_out = ~(A | B);  // NOR_Gate nor_1, 16 bits wide
  assign not_1_out = ~A;  // NOT_Gate not_1, 16 bits wide
  Multiplexer #(.select(4), .width(16)) multiplexer_1 (
    .in1({16{1'b0}}), .in2(A), .in3(B), .in4(adder_1_out), .in5(subtractor_1_out), .in6(and_1_out),
    .in7(or_1_out), .in8(xor_1_out), .in9(nand_1_out), .in10(nor_1_out), .in11(not_1_out), .out(OUTPUT),
    .sel(OPCODE));  // open: in0, in12, in13, in14, in15, en
endmodule
